// Logisim project coders.circ as structural Verilog
module Decoder (
  input  X0,
  input  X1,
  output Output0,
  output Output1,
  output Output2,
  output Output3
);

  wire not_1_out, not_2_out;

  not not_1 (not_1_out, X0);
  not not_2 (not_2_out, X1);
  and and_1 (Output0, not_1_out, not_2_out);
  and and_2 (Output1, X0, not_2_out);
  and and_3 (Output2, not_1_out, X1);
  and and_4 (Output3, X0, X1);
endmodule

module Encoder (
  input  Input0,
  input  Input1,
  input  Input2,
  input  Input3,
  output X0,
  output X1
);

  wire and_1_out, and_2_out, not_1_out, not_2_out, not_3_out;

  not not_1 (not_1_out, Input2);
  not not_2 (not_2_out, Input3);
  not not_3 (not_3_out, Input3);
  and and_1 (and_1_out, not_1_out, Input1, not_2_out);
  and and_2 (and_2_out, Input2, not_3_out);
  or or_1 (X0, and_1_out, Input3);
  or or_2 (X1, and_2_out, Input3);
endmodule

module Identity (
  input  X0,
  input  X1,
  output X0_2,
  output X1_2
);

  wire and_1_out, and_2_out, and_3_out, and_4_out, and_5_out, and_6_out, not_1_out, not_2_out, not_3_out,
       not_4_out, not_5_out;

  not not_1 (not_1_out, X0);
  not not_2 (not_2_out, X1);
  and and_1 (and_1_out, not_1_out, not_2_out);
  and and_2 (and_2_out, X0, not_2_out);
  and and_3 (and_3_out, not_1_out, X1);
  and and_4 (and_4_out, X0, X1);
  not not_3 (not_3_out, and_3_out);
  not not_4 (not_4_out, and_4_out);
  not not_5 (not_5_out, and_4_out);
  and and_5 (and_5_out, not_3_out, and_2_out, not_4_out);
  and and_6 (and_6_out, and_3_out, not_5_out);
  or or_1 (X0_2, and_5_out, and_4_out);
  or or_2 (X1_2, and_6_out, and_4_out);
endmodule
