// Logisim project dist-2.circ as structural Verilog: 1 circuit, main circuit main
module main (
  input  A,
  input  B,
  input  C,
  output out_4,
  output out_5
);

  wire and_1_out, or_1_out, or_2_out;

  or or_1 (or_1_out, A, B);
  or or_2 (or_2_out, A, C);
  and and_1 (and_1_out, B, C);
  or or_3 (out_4, A, and_1_out);
  and and_2 (out_5, or_1_out, or_2_out);
endmodule
