// Logisim project myFirst.circ as structural Verilog
module myFirst (
  input  in_1,
  output out_2
);

  wire nand_1_out, nor_1_out, not_1_out;

  not not_1 (not_1_out, in_1);
  nand nand_1 (nand_1_out, in_1, not_1_out);
  not nor_1 (nor_1_out, in_1);  // NOR_Gate
  ExactlyOne xor_1 (.out(out_2), .in0(nand_1_out), .in1(nand_1_out), .in3(nor_1_out), .in4(nor_1_out));
endmodule
