// Logisim project univ.circ as structural Verilog
module NOT (
  input  A,
  input  B,
  output out_3
);

  nand nand_1 (out_3, A, B, B);
endmodule

module AND (
  input  A,
  input  B,
  output out_3
);

  wire nand_1_out;

  nand nand_1 (nand_1_out, A, B);
  not not_1 (out_3, nand_1_out);
endmodule

module OR (
  input  A,
  input  B,
  output out_3
);

  wire not_1_out, not_2_out;

  not not_1 (not_1_out, A);
  not not_2 (not_2_out, B);
  nand nand_1 (out_3, not_1_out, not_2_out);
endmodule
