// Logisim project mux-4.circ as structural Verilog
module mux_4i (
  input  In0,
  input  In1,
  input  In2,
  input  In3,
  input  S1,
  input  S2,
  output out_7
);

  wire and_1_out, and_2_out, and_3_out, and_4_out, not_1_out, not_2_out, not_3_out, not_4_out;

  not not_1 (not_1_out, S1);
  not not_2 (not_2_out, S1);
  not not_3 (not_3_out, S2);
  and and_1 (and_1_out, In0, not_4_out);
  not not_4 (not_4_out, S2);
  and and_2 (and_2_out, In1, not_2_out);
  and and_3 (and_3_out, In2, S1);
  and and_4 (and_4_out, In3, S1);
  or or_1 (out_7, and_1_out, and_2_out, and_3_out, and_4_out);
endmodule

module mux_4ii (
  input  In0,
  input  In1,
  input  In2,
  input  In3,
  input  S0,
  input  S1,
  output Out
);

  wire main_1_out_4, main_2_out_4;

  mux_2_main main_1 (.In0(In0), .In1(In1), .in_3(S1), .out_4(main_1_out_4));
  mux_2_main main_2 (.In0(In2), .In1(In3), .in_3(S1), .out_4(main_2_out_4));
  mux_2_main main_3 (.In0(main_1_out_4), .In1(main_2_out_4), .in_3(S0), .out_4(Out));

  // Notes on the sheet:
  //   S
endmodule

module mux_2_8 (
  input  [6:0] A,
  input  [6:0] in_2,
  input  [6:0] in_3,
  output out_4,
  output out_5,
  output out_6
);

  wire and_1_out, and_2_out, and_3_out, and_4_out, and_5_out, and_6_out, not_1_out, not_2_out, not_3_out,
       not_4_out, not_5_out, not_6_out, not_7_out, not_8_out, not_9_out;

  not not_1 (not_1_out, A[6]);
  not not_2 (not_2_out, in_2[6]);
  not not_3 (not_3_out, A[5]);
  and and_1 (and_1_out, not_1_out, not_2_out, in_3[6]);
  not not_4 (not_4_out, in_3[5]);
  not not_5 (not_5_out, A[4]);
  and and_2 (and_2_out, not_3_out, not_4_out, in_2[5]);
  and and_3 (and_3_out, not_5_out, in_2[4], in_3[4]);
  not not_6 (not_6_out, in_3[3]);
  not not_7 (not_7_out, in_2[3]);
  and and_4 (and_4_out, not_7_out, A[3], not_6_out);
  not not_8 (not_8_out, in_2[2]);
  and and_5 (and_5_out, A[2], not_8_out, in_3[2]);
  not not_9 (not_9_out, in_3[1]);
  and and_6 (and_6_out, A[1], in_2[1], not_9_out);
  and and_7 (out_6, in_2[0], A[0], in_3[0]);
  or or_1 (out_4, and_1_out, out_6, and_6_out, and_5_out, and_4_out, and_3_out);
  or or_2 (out_5, and_3_out, and_5_out, and_6_out);

  // Notes on the sheet:
  //   B
  //   S
  //   A
endmodule

module fa_1 (
  input  A,
  input  B,
  input  C,
  output Carry,
  output Sum
);

  wire and_1_out, and_2_out, xor_1_out;

  and and_1 (and_1_out, A, B);
  xor xor_1 (xor_1_out, A, B);
  and and_2 (and_2_out, xor_1_out, C);
  xor xor_2 (Sum, xor_1_out, C);
  or or_1 (Carry, and_1_out, and_2_out);

  // Notes on the sheet:
  //   Carry1
  //   Sum1
  //   Carry2
  //   Sum2
endmodule

module fa_4 (
  input  A,
  input  B,
  input  A_2,
  input  B_2,
  input  A_3,
  input  B_3,
  input  A_4,
  input  B_4,
  input  Carry0,
  output Carry4,
  output Sum4,
  output Sum3,
  output Sum2,
  output Sum1
);

  wire and_1_out, and_2_out, and_3_out, and_4_out, and_5_out, and_6_out, and_7_out, and_8_out, or_1_out,
       or_2_out, or_3_out, xor_1_out, xor_3_out, xor_5_out, xor_7_out;

  and and_1 (and_1_out, A_4, B_4);
  xor xor_1 (xor_1_out, A_4, B_4);
  and and_2 (and_2_out, xor_1_out, Carry0);
  xor xor_2 (Sum1, xor_1_out, Carry0);
  or or_1 (or_1_out, and_1_out, and_2_out);
  and and_3 (and_3_out, A_3, B_3);
  xor xor_3 (xor_3_out, A_3, B_3);
  and and_4 (and_4_out, xor_3_out, or_1_out);
  xor xor_4 (Sum2, xor_3_out, or_1_out);
  or or_2 (or_2_out, and_3_out, and_4_out);
  and and_5 (and_5_out, A_2, B_2);
  xor xor_5 (xor_5_out, A_2, B_2);
  and and_6 (and_6_out, xor_5_out, or_2_out);
  xor xor_6 (Sum3, xor_5_out, or_2_out);
  or or_3 (or_3_out, and_5_out, and_6_out);
  and and_7 (and_7_out, A, B);
  xor xor_7 (xor_7_out, A, B);
  and and_8 (and_8_out, xor_7_out, or_3_out);
  xor xor_8 (Sum4, xor_7_out, or_3_out);
  or or_4 (Carry4, and_7_out, and_8_out);

  // Notes on the sheet:
  //   Carry1
  //   Carry2
  //   Carry3
endmodule

module alu_1 (
  input  Operation,
  input  in_2,
  input  in_3,
  input  A,
  input  B,
  output out_6,
  output CarryOut
);

  wire and_1_out, fa_1_1_sum, or_1_out;

  and and_1 (and_1_out, A, B);
  or or_1 (or_1_out, A, B);
  fa_1 fa_1_1 (.A(A), .B(B), .C(in_3), .Carry(CarryOut), .Sum(fa_1_1_sum));
  mux_4i mux_4i_1 (
    .In0(in_2), .In1(Operation), .In2(and_1_out), .In3(or_1_out), .S1(fa_1_1_sum), .out_7(out_6));  // open: S2
endmodule
