// Logisim project Lab4Circuits.circ as structural Verilog: 6 circuits, main circuit main
module main (
  input  [1:0] Oper,
  input  AInvert,
  input  BNegate,
  input  Less,
  input  [31:0] B,
  input  [31:0] B_2,
  output EqualZero,
  output [31:0] Result,
  output CarryOut
);

  wire alu_1bit_slt_1_carryout, alu_1bit_slt_2_carryout, alu_1bit_slt_3_carryout, alu_1bit_slt_4_carryout,
       alu_1bit_slt_5_carryout, alu_1bit_slt_6_carryout, alu_1bit_slt_7_carryout, alu_1bit_slt_8_carryout,
       alu_1bit_slt_9_p7, alu_1bit_slt_10_carryout, alu_1bit_slt_11_carryout, alu_1bit_slt_12_carryout,
       alu_1bit_slt_13_carryout, alu_1bit_slt_14_carryout, alu_1bit_slt_15_carryout,
       alu_1bit_slt_16_carryout, alu_1bit_slt_17_carryout, alu_1bit_slt_18_carryout,
       alu_1bit_slt_19_carryout, alu_1bit_slt_20_carryout, alu_1bit_slt_21_carryout,
       alu_1bit_slt_22_carryout, alu_1bit_slt_23_carryout, alu_1bit_slt_24_carryout,
       alu_1bit_slt_25_carryout, alu_1bit_slt_26_carryout, alu_1bit_slt_27_carryout,
       alu_1bit_slt_28_carryout, alu_1bit_slt_29_carryout, alu_1bit_slt_30_carryout,
       alu_1bit_slt_31_carryout, alu_1bit_slt_32_set, or_1_out;

  alu_1bit_slt alu_1bit_slt_1 (
    .A(B[0]), .B(B_2[0]), .Less(alu_1bit_slt_32_set), .AInvert(AInvert), .BInvert(BNegate),
    .CarryIn(BNegate), .Op1(Oper[1]), .Op0(Oper[0]), .CarryOut(alu_1bit_slt_1_carryout), .Result(Result[0]));  // open: Set, Overflow
  alu_1bit_slt alu_1bit_slt_2 (
    .A(B[1]), .B(B_2[1]), .Less(Less), .AInvert(AInvert), .BInvert(BNegate),
    .CarryIn(alu_1bit_slt_1_carryout), .Op1(Oper[1]), .Op0(Oper[0]), .CarryOut(alu_1bit_slt_2_carryout),
    .Result(Result[1]));  // open: Set, Overflow
  alu_1bit_slt alu_1bit_slt_3 (
    .A(B[2]), .B(B_2[2]), .Less(Less), .AInvert(AInvert), .BInvert(BNegate),
    .CarryIn(alu_1bit_slt_2_carryout), .Op1(Oper[1]), .Op0(Oper[0]), .CarryOut(alu_1bit_slt_3_carryout),
    .Result(Result[2]));  // open: Set, Overflow
  alu_1bit_slt alu_1bit_slt_4 (
    .A(B[3]), .B(B_2[3]), .Less(Less), .AInvert(AInvert), .BInvert(BNegate),
    .CarryIn(alu_1bit_slt_3_carryout), .Op1(Oper[1]), .Op0(Oper[0]), .CarryOut(alu_1bit_slt_4_carryout),
    .Result(Result[3]));  // open: Set, Overflow
  alu_1bit_slt alu_1bit_slt_5 (
    .A(B[4]), .B(B_2[4]), .Less(Less), .AInvert(AInvert), .BInvert(BNegate),
    .CarryIn(alu_1bit_slt_4_carryout), .Op1(Oper[1]), .Op0(Oper[0]), .CarryOut(alu_1bit_slt_5_carryout),
    .Result(Result[4]));  // open: Set, Overflow
  alu_1bit_slt alu_1bit_slt_6 (
    .A(B[5]), .B(B_2[5]), .Less(Less), .AInvert(AInvert), .BInvert(BNegate),
    .CarryIn(alu_1bit_slt_5_carryout), .Op1(Oper[1]), .Op0(Oper[0]), .CarryOut(alu_1bit_slt_6_carryout),
    .Result(Result[5]));  // open: Set, Overflow
  alu_1bit_slt alu_1bit_slt_7 (
    .A(B[6]), .B(B_2[6]), .Less(Less), .AInvert(AInvert), .BInvert(BNegate),
    .CarryIn(alu_1bit_slt_6_carryout), .Op1(Oper[1]), .Op0(Oper[0]), .CarryOut(alu_1bit_slt_7_carryout),
    .Result(Result[6]));  // open: Set, Overflow
  alu_1bit_slt alu_1bit_slt_8 (
    .A(B[7]), .B(B_2[7]), .Less(Less), .AInvert(AInvert), .BInvert(BNegate),
    .CarryIn(alu_1bit_slt_7_carryout), .Op1(Oper[1]), .Op0(Oper[0]), .CarryOut(alu_1bit_slt_8_carryout),
    .Result(Result[7]));  // open: Set, Overflow
  // alu_1bit_slt alu_1bit_slt_9: pin names not known; wires that end beside it: B[8], B_2[8], Less, AInvert, BNegate, alu_1bit_slt_8_carryout, alu_1bit_slt_9_p7, Oper[1], Oper[0], Result[8]
  alu_1bit_slt alu_1bit_slt_10 (
    .A(B[9]), .B(B_2[9]), .Less(Less), .AInvert(AInvert), .BInvert(BNegate), .CarryIn(alu_1bit_slt_9_p7),
    .Op1(Oper[1]), .Op0(Oper[0]), .CarryOut(alu_1bit_slt_10_carryout), .Result(Result[9]));  // open: Set, Overflow
  alu_1bit_slt alu_1bit_slt_11 (
    .A(B[10]), .B(B_2[10]), .Less(Less), .AInvert(AInvert), .BInvert(BNegate),
    .CarryIn(alu_1bit_slt_10_carryout), .Op1(Oper[1]), .Op0(Oper[0]), .CarryOut(alu_1bit_slt_11_carryout),
    .Result(Result[10]));  // open: Set, Overflow
  alu_1bit_slt alu_1bit_slt_12 (
    .A(B[11]), .B(B_2[11]), .Less(Less), .AInvert(AInvert), .BInvert(BNegate),
    .CarryIn(alu_1bit_slt_11_carryout), .Op1(Oper[1]), .Op0(Oper[0]), .CarryOut(alu_1bit_slt_12_carryout),
    .Result(Result[11]));  // open: Set, Overflow
  alu_1bit_slt alu_1bit_slt_13 (
    .A(B[12]), .B(B_2[12]), .Less(Less), .AInvert(AInvert), .BInvert(BNegate),
    .CarryIn(alu_1bit_slt_12_carryout), .Op1(Oper[1]), .Op0(Oper[0]), .CarryOut(alu_1bit_slt_13_carryout),
    .Result(Result[12]));  // open: Set, Overflow
  alu_1bit_slt alu_1bit_slt_14 (
    .A(B[13]), .B(B_2[13]), .Less(Less), .AInvert(AInvert), .BInvert(BNegate),
    .CarryIn(alu_1bit_slt_13_carryout), .Op1(Oper[1]), .Op0(Oper[0]), .CarryOut(alu_1bit_slt_14_carryout),
    .Result(Result[13]));  // open: Set, Overflow
  alu_1bit_slt alu_1bit_slt_15 (
    .A(B[14]), .B(B_2[14]), .Less(Less), .AInvert(AInvert), .BInvert(BNegate),
    .CarryIn(alu_1bit_slt_14_carryout), .Op1(Oper[1]), .Op0(Oper[0]), .CarryOut(alu_1bit_slt_15_carryout),
    .Result(Result[14]));  // open: Set, Overflow
  alu_1bit_slt alu_1bit_slt_16 (
    .A(B[15]), .B(B_2[15]), .Less(Less), .AInvert(AInvert), .BInvert(BNegate),
    .CarryIn(alu_1bit_slt_15_carryout), .Op1(Oper[1]), .Op0(Oper[0]), .CarryOut(alu_1bit_slt_16_carryout),
    .Result(Result[15]));  // open: Set, Overflow
  alu_1bit_slt alu_1bit_slt_17 (
    .A(B[16]), .B(B_2[16]), .Less(Less), .AInvert(AInvert), .BInvert(BNegate),
    .CarryIn(alu_1bit_slt_16_carryout), .Op1(Oper[1]), .Op0(Oper[0]), .CarryOut(alu_1bit_slt_17_carryout),
    .Result(Result[16]));  // open: Set, Overflow
  alu_1bit_slt alu_1bit_slt_18 (
    .A(B[17]), .B(B_2[17]), .Less(Less), .AInvert(AInvert), .BInvert(BNegate),
    .CarryIn(alu_1bit_slt_17_carryout), .Op1(Oper[1]), .Op0(Oper[0]), .CarryOut(alu_1bit_slt_18_carryout),
    .Result(Result[17]));  // open: Set, Overflow
  alu_1bit_slt alu_1bit_slt_19 (
    .A(B[18]), .B(B_2[18]), .Less(Less), .AInvert(AInvert), .BInvert(BNegate),
    .CarryIn(alu_1bit_slt_18_carryout), .Op1(Oper[1]), .Op0(Oper[0]), .CarryOut(alu_1bit_slt_19_carryout),
    .Result(Result[18]));  // open: Set, Overflow
  alu_1bit_slt alu_1bit_slt_20 (
    .A(B[19]), .B(B_2[19]), .Less(Less), .AInvert(AInvert), .BInvert(BNegate),
    .CarryIn(alu_1bit_slt_19_carryout), .Op1(Oper[1]), .Op0(Oper[0]), .CarryOut(alu_1bit_slt_20_carryout),
    .Result(Result[19]));  // open: Set, Overflow
  alu_1bit_slt alu_1bit_slt_21 (
    .A(B[20]), .B(B_2[20]), .Less(Less), .AInvert(AInvert), .BInvert(BNegate),
    .CarryIn(alu_1bit_slt_20_carryout), .Op1(Oper[1]), .Op0(Oper[0]), .CarryOut(alu_1bit_slt_21_carryout),
    .Result(Result[20]));  // open: Set, Overflow
  alu_1bit_slt alu_1bit_slt_22 (
    .A(B[21]), .B(B_2[21]), .Less(Less), .AInvert(AInvert), .BInvert(BNegate),
    .CarryIn(alu_1bit_slt_21_carryout), .Op1(Oper[1]), .Op0(Oper[0]), .CarryOut(alu_1bit_slt_22_carryout),
    .Result(Result[21]));  // open: Set, Overflow
  alu_1bit_slt alu_1bit_slt_23 (
    .A(B[22]), .B(B_2[22]), .Less(Less), .AInvert(AInvert), .BInvert(BNegate),
    .CarryIn(alu_1bit_slt_22_carryout), .Op1(Oper[1]), .Op0(Oper[0]), .CarryOut(alu_1bit_slt_23_carryout),
    .Result(Result[22]));  // open: Set, Overflow
  alu_1bit_slt alu_1bit_slt_24 (
    .A(B[23]), .B(B_2[23]), .Less(Less), .AInvert(AInvert), .BInvert(BNegate),
    .CarryIn(alu_1bit_slt_23_carryout), .Op1(Oper[1]), .Op0(Oper[0]), .CarryOut(alu_1bit_slt_24_carryout),
    .Result(Result[23]));  // open: Set, Overflow
  alu_1bit_slt alu_1bit_slt_25 (
    .A(B[24]), .B(B_2[24]), .Less(Less), .AInvert(AInvert), .BInvert(BNegate),
    .CarryIn(alu_1bit_slt_24_carryout), .Op1(Oper[1]), .Op0(Oper[0]), .CarryOut(alu_1bit_slt_25_carryout),
    .Result(Result[24]));  // open: Set, Overflow
  alu_1bit_slt alu_1bit_slt_26 (
    .A(B[25]), .B(B_2[25]), .Less(Less), .AInvert(AInvert), .BInvert(BNegate),
    .CarryIn(alu_1bit_slt_25_carryout), .Op1(Oper[1]), .Op0(Oper[0]), .CarryOut(alu_1bit_slt_26_carryout),
    .Result(Result[25]));  // open: Set, Overflow
  alu_1bit_slt alu_1bit_slt_27 (
    .A(B[26]), .B(B_2[26]), .Less(Less), .AInvert(AInvert), .BInvert(BNegate),
    .CarryIn(alu_1bit_slt_26_carryout), .Op1(Oper[1]), .Op0(Oper[0]), .CarryOut(alu_1bit_slt_27_carryout),
    .Result(Result[26]));  // open: Set, Overflow
  alu_1bit_slt alu_1bit_slt_28 (
    .A(B[27]), .B(B_2[27]), .Less(Less), .AInvert(AInvert), .BInvert(BNegate),
    .CarryIn(alu_1bit_slt_27_carryout), .Op1(Oper[1]), .Op0(Oper[0]), .CarryOut(alu_1bit_slt_28_carryout),
    .Result(Result[27]));  // open: Set, Overflow
  alu_1bit_slt alu_1bit_slt_29 (
    .A(B[28]), .B(B_2[28]), .Less(Less), .AInvert(AInvert), .BInvert(BNegate),
    .CarryIn(alu_1bit_slt_28_carryout), .Op1(Oper[1]), .Op0(Oper[0]), .CarryOut(alu_1bit_slt_29_carryout),
    .Result(Result[28]));  // open: Set, Overflow
  alu_1bit_slt alu_1bit_slt_30 (
    .A(B[29]), .B(B_2[29]), .Less(Less), .AInvert(AInvert), .BInvert(BNegate),
    .CarryIn(alu_1bit_slt_29_carryout), .Op1(Oper[1]), .Op0(Oper[0]), .CarryOut(alu_1bit_slt_30_carryout),
    .Result(Result[29]));  // open: Set, Overflow
  alu_1bit_slt alu_1bit_slt_31 (
    .A(B[30]), .B(B_2[30]), .Less(Less), .AInvert(AInvert), .BInvert(BNegate),
    .CarryIn(alu_1bit_slt_30_carryout), .Op1(Oper[1]), .Op0(Oper[0]), .CarryOut(alu_1bit_slt_31_carryout),
    .Result(Result[30]));  // open: Set, Overflow
  alu_1bit_slt alu_1bit_slt_32 (
    .A(B[31]), .B(B_2[31]), .AInvert(AInvert), .BInvert(BNegate), .CarryIn(alu_1bit_slt_31_carryout),
    .Op1(Oper[1]), .Op0(Oper[0]), .CarryOut(CarryOut), .Result(Result[31]), .Set(alu_1bit_slt_32_set));  // open: Less, Overflow
  or or_1 (or_1_out, Result[0], Result[1], Result[2], Result[3], Result[4], Result[5], Result[6], Result[7], Result[8], Result[9], Result[10], Result[11], Result[12], Result[13], Result[14], Result[15], Result[16], Result[17], Result[18], Result[19], Result[20], Result[21], Result[22], Result[23], Result[24], Result[25], Result[26], Result[27], Result[28], Result[29], Result[30], Result[31]);
  not not_1 (EqualZero, or_1_out);
endmodule

module alu_32bit_mips (
  input  [1:0] Oper,
  input  AInvert,
  input  BNegate,
  input  Less,
  input  [31:0] B,
  input  [31:0] B_2,
  output EqualZero,
  output [31:0] Result,
  output CarryOut
);

  wire alu_1bit_slt_1_carryout, alu_1bit_slt_2_carryout, alu_1bit_slt_3_carryout, alu_1bit_slt_4_carryout,
       alu_1bit_slt_5_carryout, alu_1bit_slt_6_carryout, alu_1bit_slt_7_carryout, alu_1bit_slt_8_carryout,
       alu_1bit_slt_9_p7, alu_1bit_slt_10_carryout, alu_1bit_slt_11_carryout, alu_1bit_slt_12_carryout,
       alu_1bit_slt_13_carryout, alu_1bit_slt_14_carryout, alu_1bit_slt_15_carryout,
       alu_1bit_slt_16_carryout, alu_1bit_slt_17_carryout, alu_1bit_slt_18_carryout,
       alu_1bit_slt_19_carryout, alu_1bit_slt_20_carryout, alu_1bit_slt_21_carryout,
       alu_1bit_slt_22_carryout, alu_1bit_slt_23_carryout, alu_1bit_slt_24_carryout,
       alu_1bit_slt_25_carryout, alu_1bit_slt_26_carryout, alu_1bit_slt_27_carryout,
       alu_1bit_slt_28_carryout, alu_1bit_slt_29_carryout, alu_1bit_slt_30_carryout,
       alu_1bit_slt_31_carryout, alu_1bit_slt_32_set, or_1_out;

  alu_1bit_slt alu_1bit_slt_1 (
    .A(B[0]), .B(B_2[0]), .Less(alu_1bit_slt_32_set), .AInvert(AInvert), .BInvert(BNegate),
    .CarryIn(BNegate), .Op1(Oper[1]), .Op0(Oper[0]), .CarryOut(alu_1bit_slt_1_carryout), .Result(Result[0]));  // open: Set, Overflow
  alu_1bit_slt alu_1bit_slt_2 (
    .A(B[1]), .B(B_2[1]), .Less(Less), .AInvert(AInvert), .BInvert(BNegate),
    .CarryIn(alu_1bit_slt_1_carryout), .Op1(Oper[1]), .Op0(Oper[0]), .CarryOut(alu_1bit_slt_2_carryout),
    .Result(Result[1]));  // open: Set, Overflow
  alu_1bit_slt alu_1bit_slt_3 (
    .A(B[2]), .B(B_2[2]), .Less(Less), .AInvert(AInvert), .BInvert(BNegate),
    .CarryIn(alu_1bit_slt_2_carryout), .Op1(Oper[1]), .Op0(Oper[0]), .CarryOut(alu_1bit_slt_3_carryout),
    .Result(Result[2]));  // open: Set, Overflow
  alu_1bit_slt alu_1bit_slt_4 (
    .A(B[3]), .B(B_2[3]), .Less(Less), .AInvert(AInvert), .BInvert(BNegate),
    .CarryIn(alu_1bit_slt_3_carryout), .Op1(Oper[1]), .Op0(Oper[0]), .CarryOut(alu_1bit_slt_4_carryout),
    .Result(Result[3]));  // open: Set, Overflow
  alu_1bit_slt alu_1bit_slt_5 (
    .A(B[4]), .B(B_2[4]), .Less(Less), .AInvert(AInvert), .BInvert(BNegate),
    .CarryIn(alu_1bit_slt_4_carryout), .Op1(Oper[1]), .Op0(Oper[0]), .CarryOut(alu_1bit_slt_5_carryout),
    .Result(Result[4]));  // open: Set, Overflow
  alu_1bit_slt alu_1bit_slt_6 (
    .A(B[5]), .B(B_2[5]), .Less(Less), .AInvert(AInvert), .BInvert(BNegate),
    .CarryIn(alu_1bit_slt_5_carryout), .Op1(Oper[1]), .Op0(Oper[0]), .CarryOut(alu_1bit_slt_6_carryout),
    .Result(Result[5]));  // open: Set, Overflow
  alu_1bit_slt alu_1bit_slt_7 (
    .A(B[6]), .B(B_2[6]), .Less(Less), .AInvert(AInvert), .BInvert(BNegate),
    .CarryIn(alu_1bit_slt_6_carryout), .Op1(Oper[1]), .Op0(Oper[0]), .CarryOut(alu_1bit_slt_7_carryout),
    .Result(Result[6]));  // open: Set, Overflow
  alu_1bit_slt alu_1bit_slt_8 (
    .A(B[7]), .B(B_2[7]), .Less(Less), .AInvert(AInvert), .BInvert(BNegate),
    .CarryIn(alu_1bit_slt_7_carryout), .Op1(Oper[1]), .Op0(Oper[0]), .CarryOut(alu_1bit_slt_8_carryout),
    .Result(Result[7]));  // open: Set, Overflow
  // alu_1bit_slt alu_1bit_slt_9: pin names not known; wires that end beside it: B[8], B_2[8], Less, AInvert, BNegate, alu_1bit_slt_8_carryout, alu_1bit_slt_9_p7, Oper[1], Oper[0], Result[8]
  alu_1bit_slt alu_1bit_slt_10 (
    .A(B[9]), .B(B_2[9]), .Less(Less), .AInvert(AInvert), .BInvert(BNegate), .CarryIn(alu_1bit_slt_9_p7),
    .Op1(Oper[1]), .Op0(Oper[0]), .CarryOut(alu_1bit_slt_10_carryout), .Result(Result[9]));  // open: Set, Overflow
  alu_1bit_slt alu_1bit_slt_11 (
    .A(B[10]), .B(B_2[10]), .Less(Less), .AInvert(AInvert), .BInvert(BNegate),
    .CarryIn(alu_1bit_slt_10_carryout), .Op1(Oper[1]), .Op0(Oper[0]), .CarryOut(alu_1bit_slt_11_carryout),
    .Result(Result[10]));  // open: Set, Overflow
  alu_1bit_slt alu_1bit_slt_12 (
    .A(B[11]), .B(B_2[11]), .Less(Less), .AInvert(AInvert), .BInvert(BNegate),
    .CarryIn(alu_1bit_slt_11_carryout), .Op1(Oper[1]), .Op0(Oper[0]), .CarryOut(alu_1bit_slt_12_carryout),
    .Result(Result[11]));  // open: Set, Overflow
  alu_1bit_slt alu_1bit_slt_13 (
    .A(B[12]), .B(B_2[12]), .Less(Less), .AInvert(AInvert), .BInvert(BNegate),
    .CarryIn(alu_1bit_slt_12_carryout), .Op1(Oper[1]), .Op0(Oper[0]), .CarryOut(alu_1bit_slt_13_carryout),
    .Result(Result[12]));  // open: Set, Overflow
  alu_1bit_slt alu_1bit_slt_14 (
    .A(B[13]), .B(B_2[13]), .Less(Less), .AInvert(AInvert), .BInvert(BNegate),
    .CarryIn(alu_1bit_slt_13_carryout), .Op1(Oper[1]), .Op0(Oper[0]), .CarryOut(alu_1bit_slt_14_carryout),
    .Result(Result[13]));  // open: Set, Overflow
  alu_1bit_slt alu_1bit_slt_15 (
    .A(B[14]), .B(B_2[14]), .Less(Less), .AInvert(AInvert), .BInvert(BNegate),
    .CarryIn(alu_1bit_slt_14_carryout), .Op1(Oper[1]), .Op0(Oper[0]), .CarryOut(alu_1bit_slt_15_carryout),
    .Result(Result[14]));  // open: Set, Overflow
  alu_1bit_slt alu_1bit_slt_16 (
    .A(B[15]), .B(B_2[15]), .Less(Less), .AInvert(AInvert), .BInvert(BNegate),
    .CarryIn(alu_1bit_slt_15_carryout), .Op1(Oper[1]), .Op0(Oper[0]), .CarryOut(alu_1bit_slt_16_carryout),
    .Result(Result[15]));  // open: Set, Overflow
  alu_1bit_slt alu_1bit_slt_17 (
    .A(B[16]), .B(B_2[16]), .Less(Less), .AInvert(AInvert), .BInvert(BNegate),
    .CarryIn(alu_1bit_slt_16_carryout), .Op1(Oper[1]), .Op0(Oper[0]), .CarryOut(alu_1bit_slt_17_carryout),
    .Result(Result[16]));  // open: Set, Overflow
  alu_1bit_slt alu_1bit_slt_18 (
    .A(B[17]), .B(B_2[17]), .Less(Less), .AInvert(AInvert), .BInvert(BNegate),
    .CarryIn(alu_1bit_slt_17_carryout), .Op1(Oper[1]), .Op0(Oper[0]), .CarryOut(alu_1bit_slt_18_carryout),
    .Result(Result[17]));  // open: Set, Overflow
  alu_1bit_slt alu_1bit_slt_19 (
    .A(B[18]), .B(B_2[18]), .Less(Less), .AInvert(AInvert), .BInvert(BNegate),
    .CarryIn(alu_1bit_slt_18_carryout), .Op1(Oper[1]), .Op0(Oper[0]), .CarryOut(alu_1bit_slt_19_carryout),
    .Result(Result[18]));  // open: Set, Overflow
  alu_1bit_slt alu_1bit_slt_20 (
    .A(B[19]), .B(B_2[19]), .Less(Less), .AInvert(AInvert), .BInvert(BNegate),
    .CarryIn(alu_1bit_slt_19_carryout), .Op1(Oper[1]), .Op0(Oper[0]), .CarryOut(alu_1bit_slt_20_carryout),
    .Result(Result[19]));  // open: Set, Overflow
  alu_1bit_slt alu_1bit_slt_21 (
    .A(B[20]), .B(B_2[20]), .Less(Less), .AInvert(AInvert), .BInvert(BNegate),
    .CarryIn(alu_1bit_slt_20_carryout), .Op1(Oper[1]), .Op0(Oper[0]), .CarryOut(alu_1bit_slt_21_carryout),
    .Result(Result[20]));  // open: Set, Overflow
  alu_1bit_slt alu_1bit_slt_22 (
    .A(B[21]), .B(B_2[21]), .Less(Less), .AInvert(AInvert), .BInvert(BNegate),
    .CarryIn(alu_1bit_slt_21_carryout), .Op1(Oper[1]), .Op0(Oper[0]), .CarryOut(alu_1bit_slt_22_carryout),
    .Result(Result[21]));  // open: Set, Overflow
  alu_1bit_slt alu_1bit_slt_23 (
    .A(B[22]), .B(B_2[22]), .Less(Less), .AInvert(AInvert), .BInvert(BNegate),
    .CarryIn(alu_1bit_slt_22_carryout), .Op1(Oper[1]), .Op0(Oper[0]), .CarryOut(alu_1bit_slt_23_carryout),
    .Result(Result[22]));  // open: Set, Overflow
  alu_1bit_slt alu_1bit_slt_24 (
    .A(B[23]), .B(B_2[23]), .Less(Less), .AInvert(AInvert), .BInvert(BNegate),
    .CarryIn(alu_1bit_slt_23_carryout), .Op1(Oper[1]), .Op0(Oper[0]), .CarryOut(alu_1bit_slt_24_carryout),
    .Result(Result[23]));  // open: Set, Overflow
  alu_1bit_slt alu_1bit_slt_25 (
    .A(B[24]), .B(B_2[24]), .Less(Less), .AInvert(AInvert), .BInvert(BNegate),
    .CarryIn(alu_1bit_slt_24_carryout), .Op1(Oper[1]), .Op0(Oper[0]), .CarryOut(alu_1bit_slt_25_carryout),
    .Result(Result[24]));  // open: Set, Overflow
  alu_1bit_slt alu_1bit_slt_26 (
    .A(B[25]), .B(B_2[25]), .Less(Less), .AInvert(AInvert), .BInvert(BNegate),
    .CarryIn(alu_1bit_slt_25_carryout), .Op1(Oper[1]), .Op0(Oper[0]), .CarryOut(alu_1bit_slt_26_carryout),
    .Result(Result[25]));  // open: Set, Overflow
  alu_1bit_slt alu_1bit_slt_27 (
    .A(B[26]), .B(B_2[26]), .Less(Less), .AInvert(AInvert), .BInvert(BNegate),
    .CarryIn(alu_1bit_slt_26_carryout), .Op1(Oper[1]), .Op0(Oper[0]), .CarryOut(alu_1bit_slt_27_carryout),
    .Result(Result[26]));  // open: Set, Overflow
  alu_1bit_slt alu_1bit_slt_28 (
    .A(B[27]), .B(B_2[27]), .Less(Less), .AInvert(AInvert), .BInvert(BNegate),
    .CarryIn(alu_1bit_slt_27_carryout), .Op1(Oper[1]), .Op0(Oper[0]), .CarryOut(alu_1bit_slt_28_carryout),
    .Result(Result[27]));  // open: Set, Overflow
  alu_1bit_slt alu_1bit_slt_29 (
    .A(B[28]), .B(B_2[28]), .Less(Less), .AInvert(AInvert), .BInvert(BNegate),
    .CarryIn(alu_1bit_slt_28_carryout), .Op1(Oper[1]), .Op0(Oper[0]), .CarryOut(alu_1bit_slt_29_carryout),
    .Result(Result[28]));  // open: Set, Overflow
  alu_1bit_slt alu_1bit_slt_30 (
    .A(B[29]), .B(B_2[29]), .Less(Less), .AInvert(AInvert), .BInvert(BNegate),
    .CarryIn(alu_1bit_slt_29_carryout), .Op1(Oper[1]), .Op0(Oper[0]), .CarryOut(alu_1bit_slt_30_carryout),
    .Result(Result[29]));  // open: Set, Overflow
  alu_1bit_slt alu_1bit_slt_31 (
    .A(B[30]), .B(B_2[30]), .Less(Less), .AInvert(AInvert), .BInvert(BNegate),
    .CarryIn(alu_1bit_slt_30_carryout), .Op1(Oper[1]), .Op0(Oper[0]), .CarryOut(alu_1bit_slt_31_carryout),
    .Result(Result[30]));  // open: Set, Overflow
  alu_1bit_slt alu_1bit_slt_32 (
    .A(B[31]), .B(B_2[31]), .AInvert(AInvert), .BInvert(BNegate), .CarryIn(alu_1bit_slt_31_carryout),
    .Op1(Oper[1]), .Op0(Oper[0]), .CarryOut(CarryOut), .Result(Result[31]), .Set(alu_1bit_slt_32_set));  // open: Less, Overflow
  or or_1 (or_1_out, Result[0], Result[1], Result[2], Result[3], Result[4], Result[5], Result[6], Result[7], Result[8], Result[9], Result[10], Result[11], Result[12], Result[13], Result[14], Result[15], Result[16], Result[17], Result[18], Result[19], Result[20], Result[21], Result[22], Result[23], Result[24], Result[25], Result[26], Result[27], Result[28], Result[29], Result[30], Result[31]);
  not not_1 (EqualZero, or_1_out);
endmodule

module part2 (
  input  [1:0] WriteData,
  input  Write,
  input  WriteReg,
  input  ReadReg2,
  input  ReadReg1,
  output [1:0] RegData2,
  output [1:0] RegData1
);

  wire and_1_out, and_2_out, Clock_out, decoder_1_out0, decoder_1_out1, not_1_out, not_2_out, or_1_out,
       or_2_out;
  wire [1:0] d_ff_1_q, d_ff_3_q;

  Clock Clock (.out(Clock_out));
  Decoder #(.enable("false")) decoder_1 (.out0(decoder_1_out0), .out1(decoder_1_out1), .sel(WriteReg));
  and and_1 (and_1_out, Write, decoder_1_out0);
  and and_2 (and_2_out, Write, decoder_1_out1);
  not not_1 (not_1_out, and_1_out);
  or or_1 (or_1_out, not_1_out, Clock_out);
  not not_2 (not_2_out, and_2_out);
  or or_2 (or_2_out, not_2_out, Clock_out);
  D_Flip_Flop #(.trigger("falling")) d_ff_1 (
    .clk(or_1_out), .D(WriteData[0]), .Q(d_ff_1_q[0]));  // open: Qn, preset, en, reset
  D_Flip_Flop #(.trigger("falling")) d_ff_2 (
    .clk(or_1_out), .D(WriteData[1]), .Q(d_ff_1_q[1]));  // open: Qn, preset, en, reset
  D_Flip_Flop #(.trigger("falling")) d_ff_3 (
    .clk(or_2_out), .D(WriteData[0]), .Q(d_ff_3_q[0]));  // open: Qn, preset, en, reset
  D_Flip_Flop #(.trigger("falling")) d_ff_4 (
    .clk(or_2_out), .D(WriteData[1]), .Q(d_ff_3_q[1]));  // open: Qn, preset, en, reset
  Multiplexer #(.width(2), .enable("false")) multiplexer_1 (
    .in0(d_ff_1_q), .in1(d_ff_3_q), .out(RegData2), .sel(ReadReg2));
  Multiplexer #(.width(2), .enable("false")) multiplexer_2 (
    .in0(d_ff_1_q), .in1(d_ff_3_q), .out(RegData1), .sel(ReadReg1));
endmodule

module _4Reg_32Wide_2Read_1Write (
  input  [31:0] WriteData,
  input  [1:0] WriteReg,
  input  [1:0] ReadReg2,
  input  [1:0] ReadReg1,
  input  Write,
  output [31:0] RegData2,
  output [31:0] RegData1
);

  wire and_1_out, and_2_out, and_3_out, and_4_out, Clock_out, decoder_1_out0, decoder_1_out1, decoder_1_out2,
       decoder_1_out3;
  wire [31:0] register_1_q, register_2_q, register_3_q;

  Clock Clock (.out(Clock_out));
  Decoder #(.select(2), .enable("false")) decoder_1 (
    .out0(decoder_1_out0), .out1(decoder_1_out1), .out2(decoder_1_out2), .out3(decoder_1_out3), .sel(WriteReg));
  and and_1 (and_1_out, decoder_1_out0, Write);
  and and_2 (and_2_out, decoder_1_out1, Write);
  and and_3 (and_3_out, decoder_1_out2, Write);
  and and_4 (and_4_out, decoder_1_out3, Write);
  Register #(.width(32)) register_1 (.D(WriteData), .en(and_1_out), .Q(register_1_q), .clk(Clock_out));  // open: clr
  Register #(.width(32)) register_2 (.D(WriteData), .en(and_2_out), .Q(register_2_q), .clk(Clock_out));  // open: clr
  Register #(.width(32)) register_3 (.D(WriteData), .en(and_3_out), .Q(register_3_q), .clk(Clock_out));  // open: clr
  Register #(.width(32)) register_4 (.D(WriteData), .en(and_4_out), .Q(register_3_q), .clk(Clock_out));  // open: clr
  Multiplexer #(.select(2), .width(32), .enable("false")) multiplexer_1 (
    .in0(register_1_q), .in1(register_2_q), .in2(register_3_q), .in3(register_3_q), .out(RegData2),
    .sel(ReadReg2));
  Multiplexer #(.select(2), .width(32), .enable("false")) multiplexer_2 (
    .in0(register_1_q), .in1(register_2_q), .in2(register_3_q), .in3(register_3_q), .out(RegData1),
    .sel(ReadReg1));
endmodule

module _2Flop_2Wide_2Read (
  input  ReadReg1,
  input  ReadReg2,
  output [1:0] Reg1Data,
  output [1:0] Reg2Data
);

  wire Clock_out;
  wire [1:0] d_ff_1_q, d_ff_3_q;

  Clock Clock (.out(Clock_out));
  D_Flip_Flop #(.trigger("falling")) d_ff_1 (.clk(Clock_out), .Q(d_ff_1_q[0]));  // open: D, Qn, preset, en, reset
  D_Flip_Flop #(.trigger("falling")) d_ff_2 (.clk(Clock_out), .Q(d_ff_1_q[1]));  // open: D, Qn, preset, en, reset
  D_Flip_Flop #(.trigger("falling")) d_ff_3 (.clk(Clock_out), .Q(d_ff_3_q[0]));  // open: D, Qn, preset, en, reset
  D_Flip_Flop #(.trigger("falling")) d_ff_4 (.clk(Clock_out), .Q(d_ff_3_q[1]));  // open: D, Qn, preset, en, reset
  Multiplexer #(.width(2), .enable("false")) multiplexer_1 (
    .in0(d_ff_1_q), .in1(d_ff_3_q), .out(Reg1Data), .sel(ReadReg1));
  Multiplexer #(.width(2), .enable("false")) multiplexer_2 (
    .in0(d_ff_1_q), .in1(d_ff_3_q), .out(Reg2Data), .sel(ReadReg2));
endmodule

module _2Flop_2Wide_2Read_1Write (
  input  Write,
  input  WriteReg,
  input  ReadReg1,
  input  ReadReg2,
  input  [1:0] WriteData,
  output [1:0] ReadData1,
  output [1:0] ReadData2
);

  wire and_1_out, and_2_out, Clock_out, decoder_1_out0, decoder_1_out1, not_1_out, not_2_out, or_1_out,
       or_2_out;
  wire [1:0] d_ff_1_q, d_ff_3_q;

  Clock Clock (.out(Clock_out));
  Decoder #(.enable("false")) decoder_1 (.out0(decoder_1_out0), .out1(decoder_1_out1), .sel(WriteReg));
  and and_1 (and_1_out, Write, decoder_1_out0);
  and and_2 (and_2_out, decoder_1_out1, Write);
  not not_1 (not_1_out, and_1_out);
  not not_2 (not_2_out, and_2_out);
  or or_1 (or_1_out, not_1_out, Clock_out);
  or or_2 (or_2_out, not_2_out, Clock_out);
  D_Flip_Flop #(.trigger("falling")) d_ff_1 (
    .clk(or_1_out), .D(WriteData[0]), .Q(d_ff_1_q[0]));  // open: Qn, preset, en, reset
  D_Flip_Flop #(.trigger("falling")) d_ff_2 (
    .clk(or_1_out), .D(WriteData[1]), .Q(d_ff_1_q[1]));  // open: Qn, preset, en, reset
  D_Flip_Flop #(.trigger("falling")) d_ff_3 (
    .clk(or_2_out), .D(WriteData[0]), .Q(d_ff_3_q[0]));  // open: Qn, preset, en, reset
  D_Flip_Flop #(.trigger("falling")) d_ff_4 (
    .clk(or_2_out), .D(WriteData[1]), .Q(d_ff_3_q[1]));  // open: Qn, preset, en, reset
  Multiplexer #(.width(2), .enable("false")) multiplexer_1 (
    .in0(d_ff_1_q), .in1(d_ff_3_q), .out(ReadData1), .sel(ReadReg1));
  Multiplexer #(.width(2), .enable("false")) multiplexer_2 (
    .in0(d_ff_1_q), .in1(d_ff_3_q), .out(ReadData2), .sel(ReadReg2));
endmodule
