// Logisim project ALU.circ as structural Verilog: 4 circuits, main circuit main
module main (
  input  Ainvert,
  input  Bnegate,
  input  [1:0] Oper,
  input  [31:0] A,
  input  [31:0] B,
  output Equal_Zero,
  output [31:0] Result,
  output Overflow,
  output CarryOut
);

  wire alu_1bit_1_cout, alu_1bit_2_cout, alu_1bit_3_cout, alu_1bit_4_cout, alu_1bit_5_cout, alu_1bit_6_cout,
       alu_1bit_7_cout, alu_1bit_8_cout, alu_1bit_9_cout, alu_1bit_10_cout, alu_1bit_11_cout,
       alu_1bit_12_cout, alu_1bit_13_cout, alu_1bit_14_cout, alu_1bit_15_cout, alu_1bit_16_cout,
       alu_1bit_17_cout, alu_1bit_18_cout, alu_1bit_19_cout, alu_1bit_20_cout, alu_1bit_21_cout,
       alu_1bit_22_cout, alu_1bit_23_cout, alu_1bit_24_cout, alu_1bit_25_cout, alu_1bit_26_cout,
       alu_1bit_27_cout, alu_1bit_28_cout, alu_1bit_29_cout, alu_1bit_30_cout, alu_1bit_31_cout,
       alu_1bit_32_set, or_1_out;

  alu_1bit alu_1bit_1 (
    .A(A[0]), .B(B[0]), .Less(alu_1bit_32_set), .Ainvert(Ainvert), .Binvert(Bnegate), .Cin(Bnegate),
    .Operation(Oper), .Cout(alu_1bit_1_cout), .Result(Result[0]));  // open: Set, Overflow
  alu_1bit alu_1bit_2 (
    .A(A[1]), .B(B[1]), .Less(1'b0), .Ainvert(Ainvert), .Binvert(Bnegate), .Cin(alu_1bit_1_cout),
    .Operation(Oper), .Cout(alu_1bit_2_cout), .Result(Result[1]));  // open: Set, Overflow
  alu_1bit alu_1bit_3 (
    .A(A[2]), .B(B[2]), .Less(1'b0), .Ainvert(Ainvert), .Binvert(Bnegate), .Cin(alu_1bit_2_cout),
    .Operation(Oper), .Cout(alu_1bit_3_cout), .Result(Result[2]));  // open: Set, Overflow
  alu_1bit alu_1bit_4 (
    .A(A[3]), .B(B[3]), .Less(1'b0), .Ainvert(Ainvert), .Binvert(Bnegate), .Cin(alu_1bit_3_cout),
    .Operation(Oper), .Cout(alu_1bit_4_cout), .Result(Result[3]));  // open: Set, Overflow
  alu_1bit alu_1bit_5 (
    .A(A[4]), .B(B[4]), .Less(1'b0), .Ainvert(Ainvert), .Binvert(Bnegate), .Cin(alu_1bit_4_cout),
    .Operation(Oper), .Cout(alu_1bit_5_cout), .Result(Result[4]));  // open: Set, Overflow
  alu_1bit alu_1bit_6 (
    .A(A[5]), .B(B[5]), .Less(1'b0), .Ainvert(Ainvert), .Binvert(Bnegate), .Cin(alu_1bit_5_cout),
    .Operation(Oper), .Cout(alu_1bit_6_cout), .Result(Result[5]));  // open: Set, Overflow
  alu_1bit alu_1bit_7 (
    .A(A[6]), .B(B[6]), .Less(1'b0), .Ainvert(Ainvert), .Binvert(Bnegate), .Cin(alu_1bit_6_cout),
    .Operation(Oper), .Cout(alu_1bit_7_cout), .Result(Result[6]));  // open: Set, Overflow
  alu_1bit alu_1bit_8 (
    .A(A[7]), .B(B[7]), .Less(1'b0), .Ainvert(Ainvert), .Binvert(Bnegate), .Cin(alu_1bit_7_cout),
    .Operation(Oper), .Cout(alu_1bit_8_cout), .Result(Result[7]));  // open: Set, Overflow
  alu_1bit alu_1bit_9 (
    .A(A[8]), .B(B[8]), .Less(1'b0), .Ainvert(Ainvert), .Binvert(Bnegate), .Cin(alu_1bit_8_cout),
    .Operation(Oper), .Cout(alu_1bit_9_cout), .Result(Result[8]));  // open: Set, Overflow
  alu_1bit alu_1bit_10 (
    .A(A[9]), .B(B[9]), .Less(1'b0), .Ainvert(Ainvert), .Binvert(Bnegate), .Cin(alu_1bit_9_cout),
    .Operation(Oper), .Cout(alu_1bit_10_cout), .Result(Result[9]));  // open: Set, Overflow
  alu_1bit alu_1bit_11 (
    .A(A[10]), .B(B[10]), .Less(1'b0), .Ainvert(Ainvert), .Binvert(Bnegate), .Cin(alu_1bit_10_cout),
    .Operation(Oper), .Cout(alu_1bit_11_cout), .Result(Result[10]));  // open: Set, Overflow
  alu_1bit alu_1bit_12 (
    .A(A[11]), .B(B[11]), .Less(1'b0), .Ainvert(Ainvert), .Binvert(Bnegate), .Cin(alu_1bit_11_cout),
    .Operation(Oper), .Cout(alu_1bit_12_cout), .Result(Result[11]));  // open: Set, Overflow
  alu_1bit alu_1bit_13 (
    .A(A[12]), .B(B[12]), .Less(1'b0), .Ainvert(Ainvert), .Binvert(Bnegate), .Cin(alu_1bit_12_cout),
    .Operation(Oper), .Cout(alu_1bit_13_cout), .Result(Result[12]));  // open: Set, Overflow
  alu_1bit alu_1bit_14 (
    .A(A[13]), .B(B[13]), .Less(1'b0), .Ainvert(Ainvert), .Binvert(Bnegate), .Cin(alu_1bit_13_cout),
    .Operation(Oper), .Cout(alu_1bit_14_cout), .Result(Result[13]));  // open: Set, Overflow
  alu_1bit alu_1bit_15 (
    .A(A[14]), .B(B[14]), .Less(1'b0), .Ainvert(Ainvert), .Binvert(Bnegate), .Cin(alu_1bit_14_cout),
    .Operation(Oper), .Cout(alu_1bit_15_cout), .Result(Result[14]));  // open: Set, Overflow
  alu_1bit alu_1bit_16 (
    .A(A[15]), .B(B[15]), .Less(1'b0), .Ainvert(Ainvert), .Binvert(Bnegate), .Cin(alu_1bit_15_cout),
    .Operation(Oper), .Cout(alu_1bit_16_cout), .Result(Result[15]));  // open: Set, Overflow
  alu_1bit alu_1bit_17 (
    .A(A[16]), .B(B[16]), .Less(1'b0), .Ainvert(Ainvert), .Binvert(Bnegate), .Cin(alu_1bit_16_cout),
    .Operation(Oper), .Cout(alu_1bit_17_cout), .Result(Result[16]));  // open: Set, Overflow
  alu_1bit alu_1bit_18 (
    .A(A[17]), .B(B[17]), .Less(1'b0), .Ainvert(Ainvert), .Binvert(Bnegate), .Cin(alu_1bit_17_cout),
    .Operation(Oper), .Cout(alu_1bit_18_cout), .Result(Result[17]));  // open: Set, Overflow
  alu_1bit alu_1bit_19 (
    .A(A[18]), .B(B[18]), .Less(1'b0), .Ainvert(Ainvert), .Binvert(Bnegate), .Cin(alu_1bit_18_cout),
    .Operation(Oper), .Cout(alu_1bit_19_cout), .Result(Result[18]));  // open: Set, Overflow
  alu_1bit alu_1bit_20 (
    .A(A[19]), .B(B[19]), .Less(1'b0), .Ainvert(Ainvert), .Binvert(Bnegate), .Cin(alu_1bit_19_cout),
    .Operation(Oper), .Cout(alu_1bit_20_cout), .Result(Result[19]));  // open: Set, Overflow
  alu_1bit alu_1bit_21 (
    .A(A[20]), .B(B[20]), .Less(1'b0), .Ainvert(Ainvert), .Binvert(Bnegate), .Cin(alu_1bit_20_cout),
    .Operation(Oper), .Cout(alu_1bit_21_cout), .Result(Result[20]));  // open: Set, Overflow
  alu_1bit alu_1bit_22 (
    .A(A[21]), .B(B[21]), .Less(1'b0), .Ainvert(Ainvert), .Binvert(Bnegate), .Cin(alu_1bit_21_cout),
    .Operation(Oper), .Cout(alu_1bit_22_cout), .Result(Result[21]));  // open: Set, Overflow
  alu_1bit alu_1bit_23 (
    .A(A[22]), .B(B[22]), .Less(1'b0), .Ainvert(Ainvert), .Binvert(Bnegate), .Cin(alu_1bit_22_cout),
    .Operation(Oper), .Cout(alu_1bit_23_cout), .Result(Result[22]));  // open: Set, Overflow
  alu_1bit alu_1bit_24 (
    .A(A[23]), .B(B[23]), .Less(1'b0), .Ainvert(Ainvert), .Binvert(Bnegate), .Cin(alu_1bit_23_cout),
    .Operation(Oper), .Cout(alu_1bit_24_cout), .Result(Result[23]));  // open: Set, Overflow
  alu_1bit alu_1bit_25 (
    .A(A[24]), .B(B[24]), .Less(1'b0), .Ainvert(Ainvert), .Binvert(Bnegate), .Cin(alu_1bit_24_cout),
    .Operation(Oper), .Cout(alu_1bit_25_cout), .Result(Result[24]));  // open: Set, Overflow
  alu_1bit alu_1bit_26 (
    .A(A[25]), .B(B[25]), .Less(1'b0), .Ainvert(Ainvert), .Binvert(Bnegate), .Cin(alu_1bit_25_cout),
    .Operation(Oper), .Cout(alu_1bit_26_cout), .Result(Result[25]));  // open: Set, Overflow
  alu_1bit alu_1bit_27 (
    .A(A[26]), .B(B[26]), .Less(1'b0), .Ainvert(Ainvert), .Binvert(Bnegate), .Cin(alu_1bit_26_cout),
    .Operation(Oper), .Cout(alu_1bit_27_cout), .Result(Result[26]));  // open: Set, Overflow
  alu_1bit alu_1bit_28 (
    .A(A[27]), .B(B[27]), .Less(1'b0), .Ainvert(Ainvert), .Binvert(Bnegate), .Cin(alu_1bit_27_cout),
    .Operation(Oper), .Cout(alu_1bit_28_cout), .Result(Result[27]));  // open: Set, Overflow
  alu_1bit alu_1bit_29 (
    .A(A[28]), .B(B[28]), .Less(1'b0), .Ainvert(Ainvert), .Binvert(Bnegate), .Cin(alu_1bit_28_cout),
    .Operation(Oper), .Cout(alu_1bit_29_cout), .Result(Result[28]));  // open: Set, Overflow
  alu_1bit alu_1bit_30 (
    .A(A[29]), .B(B[29]), .Less(1'b0), .Ainvert(Ainvert), .Binvert(Bnegate), .Cin(alu_1bit_29_cout),
    .Operation(Oper), .Cout(alu_1bit_30_cout), .Result(Result[29]));  // open: Set, Overflow
  alu_1bit alu_1bit_31 (
    .A(A[30]), .B(B[30]), .Less(1'b0), .Ainvert(Ainvert), .Binvert(Bnegate), .Cin(alu_1bit_30_cout),
    .Operation(Oper), .Cout(alu_1bit_31_cout), .Result(Result[30]));  // open: Set, Overflow
  alu_1bit alu_1bit_32 (
    .A(A[31]), .B(B[31]), .Less(1'b0), .Ainvert(Ainvert), .Binvert(Bnegate), .Cin(alu_1bit_31_cout),
    .Operation(Oper), .Cout(CarryOut), .Result(Result[31]), .Set(alu_1bit_32_set), .Overflow(Overflow));
  or or_1 (or_1_out, Result[0], Result[1], Result[2], Result[3], Result[4], Result[5], Result[6], Result[7], Result[8], Result[9], Result[10], Result[11], Result[12], Result[13], Result[14], Result[15], Result[16], Result[17], Result[18], Result[19], Result[20], Result[21], Result[22], Result[23], Result[24], Result[25], Result[26], Result[27], Result[28], Result[29], Result[30], Result[31]);
  not not_1 (Equal_Zero, or_1_out);

  // Notes on the sheet:
  //   Less
endmodule

module alu_1bit (
  input  Ainvert,
  input  Binvert,
  input  Cin,
  input  [1:0] Operation,
  input  A,
  input  B,
  input  Less,
  output Result,
  output Set,
  output Overflow,
  output Cout
);

  wire adder_1bit_1_sum, and_1_out, multiplexer_1_out, multiplexer_2_out, not_1_out, not_2_out, or_1_out;

  not not_1 (not_1_out, A);
  not not_2 (not_2_out, B);
  Multiplexer #(.enable("false")) multiplexer_1 (.in0(A), .in1(not_1_out), .out(multiplexer_1_out), .sel(Ainvert));
  Multiplexer #(.enable("false")) multiplexer_2 (.in0(B), .in1(not_2_out), .out(multiplexer_2_out), .sel(Binvert));
  and and_1 (and_1_out, multiplexer_1_out, multiplexer_2_out);
  or or_1 (or_1_out, multiplexer_1_out, multiplexer_2_out);
  adder_1bit adder_1bit_1 (
    .X(multiplexer_1_out), .Y(multiplexer_2_out), .Cin(Cin), .Sum(adder_1bit_1_sum), .Cout(Cout));
  xor xor_1 (Overflow, Cin, Cout);
  Multiplexer #(.select(2), .enable("false")) multiplexer_3 (
    .in0(and_1_out), .in1(or_1_out), .in2(adder_1bit_1_sum), .in3(Less), .out(Result), .sel(Operation));
  xor xor_2 (Set, adder_1bit_1_sum, Overflow);
endmodule

module adder_1bit (
  input  X,
  input  Y,
  input  Cin,
  output Sum,
  output Cout
);

  wire and_1_out, and_2_out, xor_1_out;

  xor xor_1 (xor_1_out, X, Y);
  and and_1 (and_1_out, Y, X);
  and and_2 (and_2_out, xor_1_out, Cin);
  xor xor_2 (Sum, xor_1_out, Cin);
  or or_1 (Cout, and_2_out, and_1_out);
endmodule

module dummyalu (
  input  Ainvert,
  input  Bnegate,
  input  [1:0] Oper,
  input  [31:0] A,
  input  [31:0] B,
  output Equal_Zero,
  output [31:0] Result,
  output Overflow,
  output CarryOut
);

  wire alu_1bit_1_cout, alu_1bit_2_cout, alu_1bit_3_cout, alu_1bit_4_cout, alu_1bit_5_cout, alu_1bit_6_cout,
       alu_1bit_7_cout, alu_1bit_8_cout, alu_1bit_9_cout, alu_1bit_10_cout, alu_1bit_11_cout,
       alu_1bit_12_cout, alu_1bit_13_cout, alu_1bit_14_cout, alu_1bit_15_cout, alu_1bit_16_cout,
       alu_1bit_17_cout, alu_1bit_18_cout, alu_1bit_19_cout, alu_1bit_20_cout, alu_1bit_21_cout,
       alu_1bit_22_cout, alu_1bit_23_cout, alu_1bit_24_cout, alu_1bit_25_cout, alu_1bit_26_cout,
       alu_1bit_27_cout, alu_1bit_28_cout, alu_1bit_29_cout, alu_1bit_30_cout, alu_1bit_31_cout,
       alu_1bit_32_set, or_1_out;

  alu_1bit alu_1bit_1 (
    .A(A[0]), .B(B[0]), .Less(alu_1bit_32_set), .Ainvert(Ainvert), .Binvert(Bnegate), .Cin(Bnegate),
    .Operation(Oper), .Cout(alu_1bit_1_cout), .Result(Result[0]));  // open: Set, Overflow
  alu_1bit alu_1bit_2 (
    .A(A[1]), .B(B[1]), .Less(1'b0), .Ainvert(Ainvert), .Binvert(Bnegate), .Cin(alu_1bit_1_cout),
    .Operation(Oper), .Cout(alu_1bit_2_cout), .Result(Result[1]));  // open: Set, Overflow
  alu_1bit alu_1bit_3 (
    .A(A[2]), .B(B[2]), .Less(1'b0), .Ainvert(Ainvert), .Binvert(Bnegate), .Cin(alu_1bit_2_cout),
    .Operation(Oper), .Cout(alu_1bit_3_cout), .Result(Result[2]));  // open: Set, Overflow
  alu_1bit alu_1bit_4 (
    .A(A[3]), .B(B[3]), .Less(1'b0), .Ainvert(Ainvert), .Binvert(Bnegate), .Cin(alu_1bit_3_cout),
    .Operation(Oper), .Cout(alu_1bit_4_cout), .Result(Result[3]));  // open: Set, Overflow
  alu_1bit alu_1bit_5 (
    .A(A[4]), .B(B[4]), .Less(1'b0), .Ainvert(Ainvert), .Binvert(Bnegate), .Cin(alu_1bit_4_cout),
    .Operation(Oper), .Cout(alu_1bit_5_cout), .Result(Result[4]));  // open: Set, Overflow
  alu_1bit alu_1bit_6 (
    .A(A[5]), .B(B[5]), .Less(1'b0), .Ainvert(Ainvert), .Binvert(Bnegate), .Cin(alu_1bit_5_cout),
    .Operation(Oper), .Cout(alu_1bit_6_cout), .Result(Result[5]));  // open: Set, Overflow
  alu_1bit alu_1bit_7 (
    .A(A[6]), .B(B[6]), .Less(1'b0), .Ainvert(Ainvert), .Binvert(Bnegate), .Cin(alu_1bit_6_cout),
    .Operation(Oper), .Cout(alu_1bit_7_cout), .Result(Result[6]));  // open: Set, Overflow
  alu_1bit alu_1bit_8 (
    .A(A[7]), .B(B[7]), .Less(1'b0), .Ainvert(Ainvert), .Binvert(Bnegate), .Cin(alu_1bit_7_cout),
    .Operation(Oper), .Cout(alu_1bit_8_cout), .Result(Result[7]));  // open: Set, Overflow
  alu_1bit alu_1bit_9 (
    .A(A[8]), .B(B[8]), .Less(1'b0), .Ainvert(Ainvert), .Binvert(Bnegate), .Cin(alu_1bit_8_cout),
    .Operation(Oper), .Cout(alu_1bit_9_cout), .Result(Result[8]));  // open: Set, Overflow
  alu_1bit alu_1bit_10 (
    .A(A[9]), .B(B[9]), .Less(1'b0), .Ainvert(Ainvert), .Binvert(Bnegate), .Cin(alu_1bit_9_cout),
    .Operation(Oper), .Cout(alu_1bit_10_cout), .Result(Result[9]));  // open: Set, Overflow
  alu_1bit alu_1bit_11 (
    .A(A[10]), .B(B[10]), .Less(1'b0), .Ainvert(Ainvert), .Binvert(Bnegate), .Cin(alu_1bit_10_cout),
    .Operation(Oper), .Cout(alu_1bit_11_cout), .Result(Result[10]));  // open: Set, Overflow
  alu_1bit alu_1bit_12 (
    .A(A[11]), .B(B[11]), .Less(1'b0), .Ainvert(Ainvert), .Binvert(Bnegate), .Cin(alu_1bit_11_cout),
    .Operation(Oper), .Cout(alu_1bit_12_cout), .Result(Result[11]));  // open: Set, Overflow
  alu_1bit alu_1bit_13 (
    .A(A[12]), .B(B[12]), .Less(1'b0), .Ainvert(Ainvert), .Binvert(Bnegate), .Cin(alu_1bit_12_cout),
    .Operation(Oper), .Cout(alu_1bit_13_cout), .Result(Result[12]));  // open: Set, Overflow
  alu_1bit alu_1bit_14 (
    .A(A[13]), .B(B[13]), .Less(1'b0), .Ainvert(Ainvert), .Binvert(Bnegate), .Cin(alu_1bit_13_cout),
    .Operation(Oper), .Cout(alu_1bit_14_cout), .Result(Result[13]));  // open: Set, Overflow
  alu_1bit alu_1bit_15 (
    .A(A[14]), .B(B[14]), .Less(1'b0), .Ainvert(Ainvert), .Binvert(Bnegate), .Cin(alu_1bit_14_cout),
    .Operation(Oper), .Cout(alu_1bit_15_cout), .Result(Result[14]));  // open: Set, Overflow
  alu_1bit alu_1bit_16 (
    .A(A[15]), .B(B[15]), .Less(1'b0), .Ainvert(Ainvert), .Binvert(Bnegate), .Cin(alu_1bit_15_cout),
    .Operation(Oper), .Cout(alu_1bit_16_cout), .Result(Result[15]));  // open: Set, Overflow
  alu_1bit alu_1bit_17 (
    .A(A[16]), .B(B[16]), .Less(1'b0), .Ainvert(Ainvert), .Binvert(Bnegate), .Cin(alu_1bit_16_cout),
    .Operation(Oper), .Cout(alu_1bit_17_cout), .Result(Result[16]));  // open: Set, Overflow
  alu_1bit alu_1bit_18 (
    .A(A[17]), .B(B[17]), .Less(1'b0), .Ainvert(Ainvert), .Binvert(Bnegate), .Cin(alu_1bit_17_cout),
    .Operation(Oper), .Cout(alu_1bit_18_cout), .Result(Result[17]));  // open: Set, Overflow
  alu_1bit alu_1bit_19 (
    .A(A[18]), .B(B[18]), .Less(1'b0), .Ainvert(Ainvert), .Binvert(Bnegate), .Cin(alu_1bit_18_cout),
    .Operation(Oper), .Cout(alu_1bit_19_cout), .Result(Result[18]));  // open: Set, Overflow
  alu_1bit alu_1bit_20 (
    .A(A[19]), .B(B[19]), .Less(1'b0), .Ainvert(Ainvert), .Binvert(Bnegate), .Cin(alu_1bit_19_cout),
    .Operation(Oper), .Cout(alu_1bit_20_cout), .Result(Result[19]));  // open: Set, Overflow
  alu_1bit alu_1bit_21 (
    .A(A[20]), .B(B[20]), .Less(1'b0), .Ainvert(Ainvert), .Binvert(Bnegate), .Cin(alu_1bit_20_cout),
    .Operation(Oper), .Cout(alu_1bit_21_cout), .Result(Result[20]));  // open: Set, Overflow
  alu_1bit alu_1bit_22 (
    .A(A[21]), .B(B[21]), .Less(1'b0), .Ainvert(Ainvert), .Binvert(Bnegate), .Cin(alu_1bit_21_cout),
    .Operation(Oper), .Cout(alu_1bit_22_cout), .Result(Result[21]));  // open: Set, Overflow
  alu_1bit alu_1bit_23 (
    .A(A[22]), .B(B[22]), .Less(1'b0), .Ainvert(Ainvert), .Binvert(Bnegate), .Cin(alu_1bit_22_cout),
    .Operation(Oper), .Cout(alu_1bit_23_cout), .Result(Result[22]));  // open: Set, Overflow
  alu_1bit alu_1bit_24 (
    .A(A[23]), .B(B[23]), .Less(1'b0), .Ainvert(Ainvert), .Binvert(Bnegate), .Cin(alu_1bit_23_cout),
    .Operation(Oper), .Cout(alu_1bit_24_cout), .Result(Result[23]));  // open: Set, Overflow
  alu_1bit alu_1bit_25 (
    .A(A[24]), .B(B[24]), .Less(1'b0), .Ainvert(Ainvert), .Binvert(Bnegate), .Cin(alu_1bit_24_cout),
    .Operation(Oper), .Cout(alu_1bit_25_cout), .Result(Result[24]));  // open: Set, Overflow
  alu_1bit alu_1bit_26 (
    .A(A[25]), .B(B[25]), .Less(1'b0), .Ainvert(Ainvert), .Binvert(Bnegate), .Cin(alu_1bit_25_cout),
    .Operation(Oper), .Cout(alu_1bit_26_cout), .Result(Result[25]));  // open: Set, Overflow
  alu_1bit alu_1bit_27 (
    .A(A[26]), .B(B[26]), .Less(1'b0), .Ainvert(Ainvert), .Binvert(Bnegate), .Cin(alu_1bit_26_cout),
    .Operation(Oper), .Cout(alu_1bit_27_cout), .Result(Result[26]));  // open: Set, Overflow
  alu_1bit alu_1bit_28 (
    .A(A[27]), .B(B[27]), .Less(1'b0), .Ainvert(Ainvert), .Binvert(Bnegate), .Cin(alu_1bit_27_cout),
    .Operation(Oper), .Cout(alu_1bit_28_cout), .Result(Result[27]));  // open: Set, Overflow
  alu_1bit alu_1bit_29 (
    .A(A[28]), .B(B[28]), .Less(1'b0), .Ainvert(Ainvert), .Binvert(Bnegate), .Cin(alu_1bit_28_cout),
    .Operation(Oper), .Cout(alu_1bit_29_cout), .Result(Result[28]));  // open: Set, Overflow
  alu_1bit alu_1bit_30 (
    .A(A[29]), .B(B[29]), .Less(1'b0), .Ainvert(Ainvert), .Binvert(Bnegate), .Cin(alu_1bit_29_cout),
    .Operation(Oper), .Cout(alu_1bit_30_cout), .Result(Result[29]));  // open: Set, Overflow
  alu_1bit alu_1bit_31 (
    .A(A[30]), .B(B[30]), .Less(1'b0), .Ainvert(Ainvert), .Binvert(Bnegate), .Cin(alu_1bit_30_cout),
    .Operation(Oper), .Cout(alu_1bit_31_cout), .Result(Result[30]));  // open: Set, Overflow
  alu_1bit alu_1bit_32 (
    .A(A[31]), .B(B[31]), .Less(1'b0), .Ainvert(Ainvert), .Binvert(Bnegate), .Cin(alu_1bit_31_cout),
    .Operation(Oper), .Cout(CarryOut), .Result(Result[31]), .Set(alu_1bit_32_set), .Overflow(Overflow));
  or or_1 (or_1_out, Result[0], Result[1], Result[2], Result[3], Result[4], Result[5], Result[6], Result[7], Result[8], Result[9], Result[10], Result[11], Result[12], Result[13], Result[14], Result[15], Result[16], Result[17], Result[18], Result[19], Result[20], Result[21], Result[22], Result[23], Result[24], Result[25], Result[26], Result[27], Result[28], Result[29], Result[30], Result[31]);
  not not_1 (Equal_Zero, or_1_out);

  // Notes on the sheet:
  //   Less
endmodule
