// Logisim project Data-Memory.circ as structural Verilog: 1 circuit, main circuit main
module main (
  input  [31:0] Address,
  input  [31:0] ReadData,
  input  [31:0] WriteData,
  input  MemWrite,
  input  Clock
);

  RAM #(.addrWidth(6), .dataWidth(32), .bus("separate")) ram_1 (
    .addr(Address[7:2]), .din(WriteData), .data(ReadData), .str(MemWrite), .clk(Clock));  // open: sel, ld, clr
endmodule
