// Logisim project Finale.circ as structural Verilog: 2 circuits, main circuit main
// bl
module main (
);

  wire and_1_out, main_7_equal_zero, main_control_1_alusrc, main_control_1_branch, main_control_1_memtoreg,
       main_control_1_memwrite, main_control_1_regdst, main_control_1_regtowrite;
  wire [1:0] main_control_1_aluop, undriven_7;
  wire [4:0] multiplexer_1_out, undriven_3, undriven_4;
  wire [5:0] undriven_5;
  wire [15:0] undriven_2;
  wire [31:0] main_3_result, main_4_regdata1, main_4_regdata2, main_5_instruction_2, main_7_result,
       main_8_result, multiplexer_2_out, multiplexer_3_out, multiplexer_4_out, undriven, undriven_6,
       undriven_8;

  PC_main main_1 (.DataInput(multiplexer_4_out), .DataOutput(undriven));  // open: Clock
  Instruction_Memory_main main_2 (
    .ReadAddress(undriven), .Instruction({undriven_5, undriven_4, undriven_3, undriven_2}));
  ALU_main main_3 (
    .B(32'h4), .A(undriven), .Result(main_3_result));  // open: Ainvert, Bnegate, Oper, CarryOut, Equal_Zero, Overflow
  Multiplexer #(.width(5), .enable("false")) multiplexer_1 (
    .in0(undriven_3), .in1(undriven_2[15:11]), .out(multiplexer_1_out), .sel(main_control_1_regdst));
  main_control main_control_1 (
    .Instruction(undriven_5), .RegDst(main_control_1_regdst), .RegtoWrite(main_control_1_regtowrite),
    .ALUSrc(main_control_1_alusrc), .MemtoReg(main_control_1_memtoreg), .MemWrite(main_control_1_memwrite),
    .Branch(main_control_1_branch), .ALUOp(main_control_1_aluop));
  Registers_main main_4 (
    .WriteData(multiplexer_3_out), .WriteReg(multiplexer_1_out[1:0]), .ReadReg2(undriven_3[1:0]),
    .ReadReg1(undriven_4[1:0]), .Write(main_control_1_regtowrite), .RegData2(main_4_regdata2),
    .RegData1(main_4_regdata1));
  Sign_Extend_main main_5 (.Instruction(undriven_2), .Instruction_2(main_5_instruction_2));
  Multiplexer #(.width(32), .enable("false")) multiplexer_2 (
    .in0(main_4_regdata2), .in1(main_5_instruction_2), .out(multiplexer_2_out), .sel(main_control_1_alusrc));
  Multiplexer #(.width(32), .enable("false")) multiplexer_3 (
    .in0(main_7_result), .in1(undriven_8), .out(multiplexer_3_out), .sel(main_control_1_memtoreg));
  Shift_left_main main_6 (.Instruction(main_5_instruction_2), .Instruction_2(undriven_6));
  ALU_main main_7 (
    .B(main_4_regdata1), .Oper(undriven_7), .A(multiplexer_2_out), .Equal_Zero(main_7_equal_zero),
    .Result(main_7_result));  // open: Ainvert, Bnegate, CarryOut, Overflow
  ALU_main main_8 (
    .B(main_3_result), .A(undriven_6), .Result(main_8_result));  // open: Ainvert, Bnegate, Oper, CarryOut, Equal_Zero, Overflow
  and and_1 (and_1_out, main_control_1_branch, main_7_equal_zero);
  Data_Memory_main main_9 (
    .Address(main_7_result), .WriteData(main_4_regdata2), .MemWrite(main_control_1_memwrite),
    .ReadData(undriven_8));  // open: Clock
  Multiplexer #(.width(32), .enable("false")) multiplexer_4 (
    .in0(main_3_result), .in1(main_8_result), .out(multiplexer_4_out), .sel(and_1_out));
endmodule

module main2 (
);

  wire and_1_out, Clock_out, main_7_p3, main_7_p4, main_control_1_alusrc, main_control_1_branch,
       main_control_1_memtoreg, main_control_1_memwrite, main_control_1_regdst, main_control_1_regtowrite;
  wire [1:0] main_control_1_aluop;
  wire [4:0] multiplexer_1_out;
  wire [31:0] main_3_result, main_4_regdata1, main_4_regdata2, main_5_instruction_2, main_7_p5, main_8_p1,
       multiplexer_2_out, multiplexer_3_out, multiplexer_4_out, regular_32bit_adder_1_result, undriven,
       undriven_2, undriven_3;

  Clock Clock (.out(Clock_out));
  PC_main main_1 (.DataInput(multiplexer_4_out), .Clock(Clock_out), .DataOutput(undriven));
  Instruction_Memory_main main_2 (.ReadAddress(undriven), .Instruction(main_8_p1));
  Adder_32_main main_3 (
    .A(undriven), .Result(main_3_result));  // open: Ainvert, Bnegate, CarryOut, Equal_Zero, Overflow
  Multiplexer #(.width(5), .enable("false")) multiplexer_1 (
    .in0(main_8_p1[20:16]), .in1(main_8_p1[15:11]), .out(multiplexer_1_out), .sel(main_control_1_regdst));
  main_control main_control_1 (
    .Instruction(main_8_p1[31:26]), .RegDst(main_control_1_regdst), .RegtoWrite(main_control_1_regtowrite),
    .ALUSrc(main_control_1_alusrc), .MemtoReg(main_control_1_memtoreg), .MemWrite(main_control_1_memwrite),
    .Branch(main_control_1_branch), .ALUOp(main_control_1_aluop));
  Registers_main main_4 (
    .WriteData(multiplexer_3_out), .WriteReg(multiplexer_1_out[1:0]), .ReadReg2(main_8_p1[17:16]),
    .ReadReg1(main_8_p1[22:21]), .Write(main_control_1_regtowrite), .RegData2(main_4_regdata2),
    .RegData1(main_4_regdata1));
  Sign_Extend_main main_5 (.Instruction(main_8_p1[15:0]), .Instruction_2(main_5_instruction_2));
  Multiplexer #(.width(32), .enable("false")) multiplexer_2 (
    .in0(main_4_regdata2), .in1(main_5_instruction_2), .out(multiplexer_2_out), .sel(main_control_1_alusrc));
  Multiplexer #(.width(32), .enable("false")) multiplexer_3 (
    .in0(main_7_p5), .in1(undriven_3), .out(multiplexer_3_out), .sel(main_control_1_memtoreg));
  Shift_left_main main_6 (.Instruction(main_5_instruction_2), .Instruction_2(undriven_2));
  // ALU_main main_7: pin names not known; wires that end beside it: main_4_regdata1, multiplexer_2_out, main_7_p3, main_7_p4, main_7_p5
  // ALU_Control_main main_8: pin names not known; wires that end beside it: main_8_p1[5:0], main_control_1_aluop, main_7_p3
  regular_32bit_adder regular_32bit_adder_1 (
    .B(main_3_result), .A(undriven_2), .Result(regular_32bit_adder_1_result));  // open: Ainvert, Bnegate, CarryOut, Equal_Zero, Overflow
  and and_1 (and_1_out, main_control_1_branch, main_7_p4);
  Data_Memory_main main_9 (
    .Address(main_7_p5), .MemWrite(main_control_1_memwrite), .Clock(Clock_out), .ReadData(undriven_3));  // open: WriteData
  Multiplexer #(.width(32), .enable("false")) multiplexer_4 (
    .in0(main_3_result), .in1(regular_32bit_adder_1_result), .out(multiplexer_4_out), .sel(and_1_out));
endmodule
