// Logisim project Instruction-Memory.circ as structural Verilog: 1 circuit, main circuit main
// Instruction Memory
module main (
  input  [31:0] ReadAddress,
  input  [31:0] Instruction
);

  ROM #(.addrWidth(6), .dataWidth(32)) rom_1 (.addr(ReadAddress[7:2]), .data(Instruction));  // open: sel
endmodule
