// Logisim project Lab3Circuits.circ as structural Verilog
// Op0
module alu_1bit_sub (
  input  BInvert,
  input  CarryIn,
  input  Op1,
  input  Op0,
  input  A,
  input  B,
  output Result,
  output CarryOut
);

  wire and_1_out, and_2_out, and_3_out, fa_1_1_sum, not_1_out, not_2_out, or_1_out, or_2_out;

  not not_1 (not_1_out, BInvert);
  not not_2 (not_2_out, B);
  and and_1 (and_1_out, not_1_out, B);
  and and_2 (and_2_out, BInvert, not_2_out);
  or or_1 (or_1_out, and_1_out, and_2_out);
  and and_3 (and_3_out, A, or_1_out);
  or or_2 (or_2_out, A, or_1_out);
  fa_1 fa_1_1 (.A(A), .B(or_1_out), .C(CarryIn), .Carry(CarryOut), .Sum(fa_1_1_sum));
  mux_4i mux_4i_1 (
    .In0(and_3_out), .In1(or_2_out), .In2(fa_1_1_sum), .Set1(Op1), .Set0(Op0), .Result(Result));  // open: In3
endmodule

module alu_1bit_slt (
  input  AInvert,
  input  BInvert,
  input  CarryIn,
  input  Op1,
  input  Op0,
  input  A,
  input  B,
  input  Less,
  output Result,
  output Set,
  output Overflow,
  output CarryOut
);

  wire and_1_out, and_2_out, and_3_out, and_4_out, and_5_out, fa_1_1_sum, not_1_out, not_2_out, not_3_out,
       not_4_out, or_1_out, or_2_out, or_3_out;

  not not_1 (not_1_out, AInvert);
  not not_2 (not_2_out, A);
  and and_1 (and_1_out, not_1_out, A);
  and and_2 (and_2_out, AInvert, not_2_out);
  not not_3 (not_3_out, BInvert);
  and and_3 (and_3_out, not_3_out, B);
  and and_4 (and_4_out, BInvert, not_4_out);
  not not_4 (not_4_out, B);
  or or_1 (or_1_out, and_1_out, and_2_out);
  or or_2 (or_2_out, and_3_out, and_4_out);
  and and_5 (and_5_out, or_1_out, or_2_out);
  or or_3 (or_3_out, or_1_out, or_2_out);
  fa_1 fa_1_1 (.A(or_1_out), .B(or_2_out), .C(CarryIn), .Carry(CarryOut), .Sum(fa_1_1_sum));
  mux_4i mux_4i_1 (
    .In0(and_5_out), .In1(or_3_out), .In2(fa_1_1_sum), .In3(Less), .Set1(Op1), .Set0(Op0), .Result(Result));
  xor xor_1 (Overflow, CarryIn, CarryOut);
  xor xor_2 (Set, CarryOut, Overflow);
endmodule

module alu_6bit_mips (
  input  AInvert,
  input  BNegate,
  input  Op1,
  input  Op0,
  input  [5:0] A,
  input  [5:0] B,
  input  Less,
  output EqualZero,
  output [5:0] Result,
  output Overflow,
  output CarryOut
);

  wire alu_1bit_slt_1_carryout, alu_1bit_slt_2_carryout, alu_1bit_slt_3_carryout, alu_1bit_slt_4_carryout,
       alu_1bit_slt_5_carryout, alu_1bit_slt_6_set;

  alu_1bit_slt alu_1bit_slt_1 (
    .A(A[0]), .B(B[0]), .Less(alu_1bit_slt_6_set), .AInvert(AInvert), .BInvert(BNegate), .CarryIn(BNegate),
    .Op1(Op1), .Op0(Op0), .CarryOut(alu_1bit_slt_1_carryout), .Result(Result[0]));  // open: Set, Overflow
  alu_1bit_slt alu_1bit_slt_2 (
    .A(A[1]), .B(B[1]), .Less(Less), .AInvert(AInvert), .BInvert(BNegate), .CarryIn(alu_1bit_slt_1_carryout),
    .Op1(Op1), .Op0(Op0), .CarryOut(alu_1bit_slt_2_carryout), .Result(Result[1]));  // open: Set, Overflow
  alu_1bit_slt alu_1bit_slt_3 (
    .A(A[2]), .B(B[2]), .Less(Less), .AInvert(AInvert), .BInvert(BNegate), .CarryIn(alu_1bit_slt_2_carryout),
    .Op1(Op1), .Op0(Op0), .CarryOut(alu_1bit_slt_3_carryout), .Result(Result[2]));  // open: Set, Overflow
  alu_1bit_slt alu_1bit_slt_4 (
    .A(A[3]), .B(B[3]), .Less(Less), .AInvert(AInvert), .BInvert(BNegate), .CarryIn(alu_1bit_slt_3_carryout),
    .Op1(Op1), .Op0(Op0), .CarryOut(alu_1bit_slt_4_carryout), .Result(Result[3]));  // open: Set, Overflow
  alu_1bit_slt alu_1bit_slt_5 (
    .A(A[4]), .B(B[4]), .Less(Less), .AInvert(AInvert), .BInvert(BNegate), .CarryIn(alu_1bit_slt_4_carryout),
    .Op1(Op1), .Op0(Op0), .CarryOut(alu_1bit_slt_5_carryout), .Result(Result[4]));  // open: Set, Overflow
  alu_1bit_slt alu_1bit_slt_6 (
    .A(A[5]), .B(B[5]), .Less(Less), .AInvert(AInvert), .BInvert(BNegate), .CarryIn(alu_1bit_slt_5_carryout),
    .Op1(Op1), .Op0(Op0), .CarryOut(CarryOut), .Result(Result[5]), .Set(alu_1bit_slt_6_set),
    .Overflow(Overflow));
  nor nor_1 (EqualZero, Result[0], Result[1], Result[2], Result[3], Result[4], Result[5]);
endmodule
