// Logisim project PC.circ as structural Verilog: 1 circuit, main circuit main
// Program Counter
module main (
  input  [31:0] DataInput,
  input  [31:0] DataOutput,
  input  Clock
);

  Register #(.width(32), .trigger("falling")) register_1 (.D(DataInput), .Q(DataOutput), .clk(Clock));  // open: en, clr
endmodule
