// Logisim project Registers.circ as structural Verilog: 1 circuit, main circuit main
module main (
  input  [31:0] WriteData,
  input  [1:0] WriteReg,
  input  [1:0] ReadReg2,
  input  [1:0] ReadReg1,
  input  Write,
  output [31:0] RegData2,
  output [31:0] RegData1
);

  wire and_1_out, and_2_out, and_3_out, and_4_out, Clock_out, decoder_1_out0, decoder_1_out1, decoder_1_out2,
       decoder_1_out3;
  wire [31:0] register_1_q, register_2_q, register_3_q;

  Clock Clock (.out(Clock_out));
  Decoder #(.select(2), .enable("false")) decoder_1 (
    .out0(decoder_1_out0), .out1(decoder_1_out1), .out2(decoder_1_out2), .out3(decoder_1_out3), .sel(WriteReg));
  and and_1 (and_1_out, decoder_1_out0, Write);
  and and_2 (and_2_out, decoder_1_out1, Write);
  and and_3 (and_3_out, decoder_1_out2, Write);
  and and_4 (and_4_out, decoder_1_out3, Write);
  Register #(.width(32)) register_1 (.D(WriteData), .en(and_1_out), .Q(register_1_q), .clk(Clock_out));  // open: clr
  Register #(.width(32)) register_2 (.D(WriteData), .en(and_2_out), .Q(register_2_q), .clk(Clock_out));  // open: clr
  Register #(.width(32)) register_3 (.D(WriteData), .en(and_3_out), .Q(register_3_q), .clk(Clock_out));  // open: clr
  Register #(.width(32)) register_4 (.D(WriteData), .en(and_4_out), .Q(register_3_q), .clk(Clock_out));  // open: clr
  Multiplexer #(.select(2), .width(32), .enable("false")) multiplexer_1 (
    .in0(register_1_q), .in1(register_2_q), .in2(register_3_q), .in3(register_3_q), .out(RegData2),
    .sel(ReadReg2));
  Multiplexer #(.select(2), .width(32), .enable("false")) multiplexer_2 (
    .in0(register_1_q), .in1(register_2_q), .in2(register_3_q), .in3(register_3_q), .out(RegData1),
    .sel(ReadReg1));
endmodule
