// Logisim project Shift-left.circ as structural Verilog: 1 circuit, main circuit main
// Shift Left
module main (
  input  [31:0] Instruction,
  input  [31:0] Instruction_2
);

  Shifter #(.width(32)) shifter_1 (.in(Instruction), .\dist (5'b00010), .out(Instruction_2));
endmodule
