// Logisim project mux-4.circ as structural Verilog
module mux_4i (
  input  In0,
  input  In1,
  input  In2,
  input  In3,
  input  Set1,
  input  Set0,
  output Result
);

  wire and_1_out, and_2_out, and_3_out, and_4_out, not_1_out, not_2_out, not_3_out, not_4_out;

  not not_1 (not_1_out, Set1);
  not not_2 (not_2_out, Set1);
  not not_3 (not_3_out, Set0);
  and and_1 (and_1_out, not_1_out, In0, not_4_out);
  not not_4 (not_4_out, Set0);
  and and_2 (and_2_out, In1, Set0, not_2_out);
  and and_3 (and_3_out, In2, not_3_out, Set1);
  and and_4 (and_4_out, Set0, In3, Set1);
  or or_1 (Result, and_1_out, and_2_out, and_3_out, and_4_out);
endmodule

module mux_4ii (
  input  In0,
  input  In1,
  input  In2,
  input  In3,
  input  S1,
  input  S0,
  output Result
);

  wire main_1_result, main_2_result;

  mux_2_main main_1 (.In0(In0), .In1(In1), .S(S0), .Result(main_1_result));
  mux_2_main main_2 (.In0(In2), .In1(In3), .S(S0), .Result(main_2_result));
  mux_2_main main_3 (.In0(main_1_result), .In1(main_2_result), .S(S1), .Result(Result));

  // Notes on the sheet:
  //   S
endmodule

module mux_2_8 (
  input  [6:0] A,
  input  [6:0] B,
  input  [6:0] C,
  output out_4,
  output out_5,
  output out_6
);

  wire and_1_out, and_2_out, and_3_out, and_4_out, and_5_out, and_6_out, not_1_out, not_2_out, not_3_out,
       not_4_out, not_5_out, not_6_out, not_7_out, not_8_out, not_9_out;

  not not_1 (not_1_out, A[6]);
  not not_2 (not_2_out, A[5]);
  not not_3 (not_3_out, B[6]);
  and and_1 (and_1_out, not_1_out, not_3_out, C[6]);
  not not_4 (not_4_out, C[5]);
  not not_5 (not_5_out, A[4]);
  and and_2 (and_2_out, not_2_out, not_4_out, B[5]);
  and and_3 (and_3_out, not_5_out, B[4], C[4]);
  not not_6 (not_6_out, C[3]);
  not not_7 (not_7_out, B[3]);
  and and_4 (and_4_out, not_7_out, A[3], not_6_out);
  not not_8 (not_8_out, B[2]);
  and and_5 (and_5_out, A[2], not_8_out, C[2]);
  not not_9 (not_9_out, C[1]);
  and and_6 (and_6_out, A[1], B[1], not_9_out);
  and and_7 (out_6, B[0], A[0], C[0]);
  or or_1 (out_4, and_1_out, out_6, and_6_out, and_5_out, and_4_out, and_3_out);
  or or_2 (out_5, and_3_out, and_5_out, and_6_out);

  // Notes on the sheet:
  //   A
endmodule

module fa_1 (
  input  A,
  input  B,
  input  C,
  output Carry,
  output Sum
);

  wire and_1_out, and_2_out, xor_1_out;

  and and_1 (and_1_out, A, B);
  xor xor_1 (xor_1_out, A, B);
  and and_2 (and_2_out, xor_1_out, C);
  xor xor_2 (Sum, xor_1_out, C);
  or or_1 (Carry, and_1_out, and_2_out);

  // Notes on the sheet:
  //   Carry1
  //   Sum1
  //   Carry2
  //   Sum2
endmodule

module fa_4 (
  input  CarryIn,
  input  [3:0] A,
  input  [3:0] B,
  output [3:0] Result,
  output CarryOut
);

  wire fa_1_1_carry, fa_1_2_carry, fa_1_3_carry;

  fa_1 fa_1_1 (.A(A[0]), .B(A[0]), .C(CarryIn), .Carry(fa_1_1_carry), .Sum(Result[0]));
  fa_1 fa_1_2 (.A(A[1]), .B(B[1]), .C(fa_1_1_carry), .Carry(fa_1_2_carry), .Sum(Result[1]));
  fa_1 fa_1_3 (.A(A[2]), .B(B[2]), .C(fa_1_2_carry), .Carry(fa_1_3_carry), .Sum(Result[2]));
  fa_1 fa_1_4 (.A(A[3]), .B(B[3]), .C(fa_1_3_carry), .Carry(CarryOut), .Sum(Result[3]));

  assign B[0] = A[0];
endmodule

module alu_1 (
  input  CarryIn,
  input  A,
  input  Op1,
  input  Op0,
  input  B,
  output Result,
  output CarryOut
);

  wire and_1_out, fa_1_1_sum, or_1_out;

  and and_1 (and_1_out, A, B);
  or or_1 (or_1_out, A, B);
  fa_1 fa_1_1 (.A(A), .B(B), .C(CarryIn), .Carry(CarryOut), .Sum(fa_1_1_sum));
  mux_4i mux_4i_1 (
    .In0(and_1_out), .In1(or_1_out), .In2(fa_1_1_sum), .Set1(Op1), .Set0(Op0), .Result(Result));  // open: In3
endmodule
